# Fritzing sketch Euclid (saved by Fritzing 0.9.3b)
breadboards: 1

parts:
  Part1 = Arduino Nano (Rev3.0)
  LED1 = smd LED [color="Green (570nm)" package="0603 [SMD]"]
  LED2 = smd LED [color="Green (570nm)" package="0603 [SMD]"]
  LED3 = smd LED [color="Green (570nm)" package="0603 [SMD]"]
  LED4 = smd LED [color="Green (570nm)" package="0603 [SMD]"]
  LED5 = smd LED [color="Green (570nm)" package="0603 [SMD]"]
  LED6 = smd LED [color="Green (570nm)" package="0603 [SMD]"]
  LED7 = smd LED [color="Green (570nm)" package="0603 [SMD]"]
  LED8 = smd LED [color="Green (570nm)" package="0603 [SMD]"]
  U1 = 3.5mm Audio Jack [package=audio-jack]
  U2 = 3.5mm Audio Jack [package=audio-jack]
  U3 = 3.5mm Audio Jack [package=audio-jack]
  U4 = 3.5mm Audio Jack [package=audio-jack]
  R9 = Resistor [tolerance=±5% resistance=100k package=THT]
  R1 = Resistor [tolerance=±5% resistance=220 package=THT]
  R2 = Resistor [tolerance=±5% resistance=220 package=THT]
  R3 = Resistor [tolerance=±5% resistance=220 package=THT]
  R4 = Resistor [tolerance=±5% resistance=220 package=THT]
  R5 = Resistor [tolerance=±5% resistance=220 package=THT]
  R6 = Resistor [tolerance=±5% resistance=220 package=THT]
  R7 = Resistor [tolerance=±5% resistance=220 package=THT]
  R8 = Resistor [tolerance=±5% resistance=220 package=THT]
  R10 = Resistor [tolerance=±5% resistance=100k package=THT]
  R11 = Resistor [tolerance=±5% resistance=10k package=THT]
  R12 = Resistor [tolerance=±5% resistance=10k package=THT]
  S1 = Momentary Switch [package=tactile-pth]
  R13 = Resistor [tolerance=±5% resistance=10k package=THT]

nets:
  GND: Part1.GND, LED1.cathode, LED2.cathode, LED3.cathode, LED4.cathode, LED5.cathode, LED6.cathode, LED7.cathode, LED8.cathode, U1.SLEEVE, U2.SLEEVE, U3.SLEEVE, U4.SLEEVE, R13.Pin_1
  N1: Part1.D2, R8.Pin_0
  N2: Part1.D3, R7.Pin_0
  N3: Part1.D4, R6.Pin_0
  N4: Part1.D5, R5.Pin_0
  N5: Part1.D6, R4.Pin_0
  N6: Part1.D7, R3.Pin_0
  N7: Part1.D8, R2.Pin_0
  N8: Part1.D9, R1.Pin_0
  N9: Part1.D10, R12.Pin_1
  N10: Part1.D11/MOSI, S1.4
  N11: Part1.D12/MISO, R9.Pin_1
  5V: Part1.VIN
  N12: Part1.5V, S1.1
  N13: Part1.A7, U2.RIGHT, R10.Pin_1
  N14: Part1.D13/SCK, R11.Pin_1
  N15: LED1.anode, R1.Pin_1
  N16: LED2.anode, R2.Pin_1
  N17: LED3.anode, R3.Pin_1
  N18: LED4.anode, R4.Pin_1
  N19: LED5.anode, R5.Pin_1
  N20: LED6.anode, R6.Pin_1
  N21: LED7.anode, R7.Pin_1
  N22: LED8.anode, R8.Pin_1
  N23: U1.RIGHT, R9.Pin_0
  N24: U3.RIGHT, R12.Pin_0
  N25: U4.RIGHT, R11.Pin_0
  N26: S1.3, R13.Pin_0

notes:
  Can also be 12 V
  Jacks
  Leds
  Button
